// Logisim project 8-bit CPU Design – Logisim Project.circ as structural Verilog: 18 circuits, main circuit Memory cell
module main (
  input  [3:0] TEST2,
  input  OE,
  input  [7:0] TEST,
  input  OE_TEST,
  input  Reset,
  output [3:0] MAR_content,
  output [3:0] Content_counter,
  output [7:0] IR_Content,
  output [7:0] MBR_Content,
  output [7:0] Reg_A_content,
  output [7:0] ALU_resulet,
  output [7:0] out_12,
  output [2:0] Content_counter_2,
  output [7:0] Reg_B_content
);

  wire CLK_out, cu_i_1_c0, cu_i_1_c1, cu_i_1_c2, cu_i_1_c3, cu_i_1_c4, cu_i_1_c5, cu_i_1_c6, cu_i_1_c7,
       cu_i_1_c8, cu_i_1_c9, cu_i_1_c10, cu_i_1_c11, cu_ii_1_c12, cu_ii_1_c13, cu_ii_1_c14, cu_ii_1_c15;
  wire [3:0] bitselector_2_out, controlled_buffer_1_out, MAR_dout;
  wire [7:0] alu_1_dout, bit_extender_1_out, bit_extender_2_out, Instruction_Registre_dout;
  wire [31:0] Decimal_Decoder_2_dout, Decimal_Decoder_3_dout, Decimal_Decoder_4_dout, Decimal_Decoder_5_dout,
       Decimal_Decoder_6_dout, Decimal_Decoder_dout;

  Clock CLK (.out(CLK_out));
  Decimal_decoudeur Decimal_Decoder (.Dout(Decimal_Decoder_dout));  // open: Din
  _7_Segment_Display u_7_segment_display_1 (
    .g(Decimal_Decoder_dout[15]), .f(Decimal_Decoder_dout[14]), .a(Decimal_Decoder_dout[13]),
    .b(Decimal_Decoder_dout[12]), .e(Decimal_Decoder_dout[31]), .d(Decimal_Decoder_dout[30]),
    .c(Decimal_Decoder_dout[29]), .dp(Decimal_Decoder_dout[28]));
  _7_Segment_Display u_7_segment_display_2 (
    .g(Decimal_Decoder_dout[11]), .f(Decimal_Decoder_dout[10]), .a(Decimal_Decoder_dout[9]),
    .b(Decimal_Decoder_dout[8]), .e(Decimal_Decoder_dout[27]), .d(Decimal_Decoder_dout[26]),
    .c(Decimal_Decoder_dout[25]), .dp(Decimal_Decoder_dout[24]));
  _7_Segment_Display u_7_segment_display_3 (
    .g(Decimal_Decoder_dout[3]), .f(Decimal_Decoder_dout[2]), .a(Decimal_Decoder_dout[1]),
    .b(Decimal_Decoder_dout[0]), .e(Decimal_Decoder_dout[19]), .d(Decimal_Decoder_dout[18]),
    .c(Decimal_Decoder_dout[17]), .dp(Decimal_Decoder_dout[16]));
  _7_Segment_Display u_7_segment_display_4 (
    .g(Decimal_Decoder_dout[7]), .f(Decimal_Decoder_dout[6]), .a(Decimal_Decoder_dout[5]),
    .b(Decimal_Decoder_dout[4]), .e(Decimal_Decoder_dout[23]), .d(Decimal_Decoder_dout[22]),
    .c(Decimal_Decoder_dout[21]), .dp(Decimal_Decoder_dout[20]));
  assign controlled_buffer_1_out = cu_i_1_c0 ? Content_counter : 4'bz;  // Controlled_Buffer controlled_buffer_1
  Counter #(.width(4), .max('h3)) counter_1 (
    .load(Reset), .D(controlled_buffer_1_out), .count(cu_i_1_c1), .Q(Content_counter), .clk(CLK_out));  // open: carry, clr
  Decimal_decoudeur Decimal_Decoder_2 (.Din(bit_extender_1_out), .Dout(Decimal_Decoder_2_dout));
  assign bit_extender_1_out = {{4{1'b0}}, Content_counter};  // Bit_Extender bit_extender_1
  Registre Instruction_Registre (
    .Clock(CLK_out), .WE(cu_i_1_c7), .Din(alu_1_dout), .OE(cu_i_1_c8), .Dout(Instruction_Registre_dout),
    .Stored_Data(IR_Content));
  Registre Registre_A (
    .Clock(CLK_out), .WE(cu_ii_1_c12), .Din(alu_1_dout), .Stored_Data(Reg_A_content));  // open: OE, Dout
  Registre Registre_B (
    .Clock(CLK_out), .WE(cu_ii_1_c13), .Din(alu_1_dout), .Stored_Data(Reg_B_content));  // open: OE, Dout
  _7_Segment_Display u_7_segment_display_5 (
    .g(Decimal_Decoder_2_dout[3]), .f(Decimal_Decoder_2_dout[2]), .a(Decimal_Decoder_2_dout[1]),
    .b(Decimal_Decoder_2_dout[0]), .e(Decimal_Decoder_2_dout[19]), .d(Decimal_Decoder_2_dout[18]),
    .c(Decimal_Decoder_2_dout[17]), .dp(Decimal_Decoder_2_dout[16]));
  _7_Segment_Display u_7_segment_display_6 (
    .g(Decimal_Decoder_3_dout[15]), .f(Decimal_Decoder_3_dout[14]), .a(Decimal_Decoder_3_dout[13]),
    .b(Decimal_Decoder_3_dout[12]), .e(Decimal_Decoder_3_dout[31]), .d(Decimal_Decoder_3_dout[30]),
    .c(Decimal_Decoder_3_dout[29]), .dp(Decimal_Decoder_3_dout[28]));
  Decimal_decoudeur Decimal_Decoder_3 (.Din(Reg_A_content), .Dout(Decimal_Decoder_3_dout));
  _7_Segment_Display u_7_segment_display_7 (
    .g(Decimal_Decoder_3_dout[11]), .f(Decimal_Decoder_3_dout[10]), .a(Decimal_Decoder_3_dout[9]),
    .b(Decimal_Decoder_3_dout[8]), .e(Decimal_Decoder_3_dout[27]), .d(Decimal_Decoder_3_dout[26]),
    .c(Decimal_Decoder_3_dout[25]), .dp(Decimal_Decoder_3_dout[24]));
  _7_Segment_Display u_7_segment_display_8 (
    .g(Decimal_Decoder_3_dout[7]), .f(Decimal_Decoder_3_dout[6]), .a(Decimal_Decoder_3_dout[5]),
    .b(Decimal_Decoder_3_dout[4]), .e(Decimal_Decoder_3_dout[23]), .d(Decimal_Decoder_3_dout[22]),
    .c(Decimal_Decoder_3_dout[21]), .dp(Decimal_Decoder_3_dout[20]));
  ALU alu_1 (
    .Reg_B(Reg_B_content), .Dout(alu_1_dout), .ALU_Result(ALU_resulet), .OE(cu_i_1_c11), .Reg_A(Reg_A_content));  // open: Carry_Out
  Decimal_decoudeur Decimal_Decoder_4 (.Din(Reg_B_content), .Dout(Decimal_Decoder_4_dout));
  BitSelector #(.group(4)) bitselector_1 (.in(Instruction_Registre_dout), .out(controlled_buffer_1_out), .sel(1'b0));
  _7_Segment_Display u_7_segment_display_9 (
    .g(Decimal_Decoder_3_dout[3]), .f(Decimal_Decoder_3_dout[2]), .a(Decimal_Decoder_3_dout[1]),
    .b(Decimal_Decoder_3_dout[0]), .e(Decimal_Decoder_3_dout[19]), .d(Decimal_Decoder_3_dout[18]),
    .c(Decimal_Decoder_3_dout[17]), .dp(Decimal_Decoder_3_dout[16]));
  _7_Segment_Display u_7_segment_display_10 (
    .g(Decimal_Decoder_4_dout[15]), .f(Decimal_Decoder_4_dout[14]), .a(Decimal_Decoder_4_dout[13]),
    .b(Decimal_Decoder_4_dout[12]), .e(Decimal_Decoder_4_dout[31]), .d(Decimal_Decoder_4_dout[30]),
    .c(Decimal_Decoder_4_dout[29]), .dp(Decimal_Decoder_4_dout[28]));
  _7_Segment_Display u_7_segment_display_11 (
    .g(Decimal_Decoder_4_dout[11]), .f(Decimal_Decoder_4_dout[10]), .a(Decimal_Decoder_4_dout[9]),
    .b(Decimal_Decoder_4_dout[8]), .e(Decimal_Decoder_4_dout[27]), .d(Decimal_Decoder_4_dout[26]),
    .c(Decimal_Decoder_4_dout[25]), .dp(Decimal_Decoder_4_dout[24]));
  _7_Segment_Display u_7_segment_display_12 (
    .g(Decimal_Decoder_4_dout[7]), .f(Decimal_Decoder_4_dout[6]), .a(Decimal_Decoder_4_dout[5]),
    .b(Decimal_Decoder_4_dout[4]), .e(Decimal_Decoder_4_dout[23]), .d(Decimal_Decoder_4_dout[22]),
    .c(Decimal_Decoder_4_dout[21]), .dp(Decimal_Decoder_4_dout[20]));
  _7_Segment_Display u_7_segment_display_13 (
    .g(Decimal_Decoder_4_dout[3]), .f(Decimal_Decoder_4_dout[2]), .a(Decimal_Decoder_4_dout[1]),
    .b(Decimal_Decoder_4_dout[0]), .e(Decimal_Decoder_4_dout[19]), .d(Decimal_Decoder_4_dout[18]),
    .c(Decimal_Decoder_4_dout[17]), .dp(Decimal_Decoder_4_dout[16]));
  LED D7 (.in(alu_1_dout[7]));
  LED D4 (.in(alu_1_dout[4]));
  LED D6 (.in(alu_1_dout[6]));
  LED D5 (.in(alu_1_dout[5]));
  assign alu_1_dout = OE_TEST ? TEST : 8'bz;  // Controlled_Buffer controlled_buffer_2
  LED D1 (.in(alu_1_dout[1]));
  LED D2 (.in(alu_1_dout[2]));
  LED D3 (.in(alu_1_dout[3]));
  LED D0 (.in(alu_1_dout[0]));
  \Addresse_Mémoire_Registre  MAR (
    .Clock(CLK_out), .WE(cu_i_1_c10), .Din(controlled_buffer_1_out), .OE(cu_i_1_c9), .Dout(MAR_dout),
    .Stored_Data(MAR_content));
  assign alu_1_dout = cu_i_1_c5 ? MBR_Content : 8'bz;  // Controlled_Buffer controlled_buffer_3
  Registre MBR (
    .Clock(CLK_out), .WE(cu_i_1_c4), .Din(alu_1_dout), .OE(cu_i_1_c6), .Dout(alu_1_dout),
    .Stored_Data(MBR_Content));
  Registre Output_Registre (
    .Clock(CLK_out), .WE(cu_ii_1_c15), .Din(alu_1_dout), .OE(cu_ii_1_c14), .Dout(alu_1_dout),
    .Stored_Data(out_12));
  Decimal_decoudeur Decimal_Decoder_5 (.Din(out_12), .Dout(Decimal_Decoder_5_dout));
  _7_Segment_Display u_7_segment_display_14 (
    .g(Decimal_Decoder_5_dout[11]), .f(Decimal_Decoder_5_dout[10]), .a(Decimal_Decoder_5_dout[9]),
    .b(Decimal_Decoder_5_dout[8]), .e(Decimal_Decoder_5_dout[27]), .d(Decimal_Decoder_5_dout[26]),
    .c(Decimal_Decoder_5_dout[25]), .dp(Decimal_Decoder_5_dout[24]));
  _7_Segment_Display u_7_segment_display_15 (
    .g(Decimal_Decoder_5_dout[15]), .f(Decimal_Decoder_5_dout[14]), .a(Decimal_Decoder_5_dout[13]),
    .b(Decimal_Decoder_5_dout[12]), .e(Decimal_Decoder_5_dout[31]), .d(Decimal_Decoder_5_dout[30]),
    .c(Decimal_Decoder_5_dout[29]), .dp(Decimal_Decoder_5_dout[28]));
  assign MAR_dout = OE ? TEST2 : 4'bz;  // Controlled_Buffer controlled_buffer_4
  _7_Segment_Display u_7_segment_display_16 (
    .g(Decimal_Decoder_5_dout[7]), .f(Decimal_Decoder_5_dout[6]), .a(Decimal_Decoder_5_dout[5]),
    .b(Decimal_Decoder_5_dout[4]), .e(Decimal_Decoder_5_dout[23]), .d(Decimal_Decoder_5_dout[22]),
    .c(Decimal_Decoder_5_dout[21]), .dp(Decimal_Decoder_5_dout[20]));
  _7_Segment_Display u_7_segment_display_17 (
    .g(Decimal_Decoder_5_dout[3]), .f(Decimal_Decoder_5_dout[2]), .a(Decimal_Decoder_5_dout[1]),
    .b(Decimal_Decoder_5_dout[0]), .e(Decimal_Decoder_5_dout[19]), .d(Decimal_Decoder_5_dout[18]),
    .c(Decimal_Decoder_5_dout[17]), .dp(Decimal_Decoder_5_dout[16]));
  LED D7_2 (.in(alu_1_dout[7]));
  LED D7_3 (.in(alu_1_dout[7]));
  LED D4_2 (.in(alu_1_dout[4]));
  LED D5_2 (.in(alu_1_dout[5]));
  LED D6_2 (.in(alu_1_dout[6]));
  LED D5_3 (.in(alu_1_dout[5]));
  LED D4_3 (.in(alu_1_dout[4]));
  LED D6_3 (.in(alu_1_dout[6]));
  LED D2_2 (.in(alu_1_dout[2]));
  LED D3_2 (.in(alu_1_dout[3]));
  LED D2_3 (.in(alu_1_dout[2]));
  LED D3_3 (.in(alu_1_dout[3]));
  LED D0_2 (.in(alu_1_dout[0]));
  LED D1_2 (.in(alu_1_dout[1]));
  LED D0_3 (.in(alu_1_dout[0]));
  LED D1_3 (.in(alu_1_dout[1]));
  RAM #(.addrWidth(4), .bus("separate")) ram_1 (
    .addr(MAR_dout), .din(alu_1_dout), .data(alu_1_dout), .str(cu_i_1_c2), .clk(CLK_out), .ld(cu_i_1_c3));  // open: sel, clr
  BitSelector #(.group(4)) bitselector_2 (.in(IR_Content), .out(bitselector_2_out), .sel(1'b1));
  Counter #(.width(3), .max('h5)) counter_2 (.Q(Content_counter_2), .clk(CLK_out));  // open: load, D, count, carry, clr
  assign bit_extender_2_out = {{5{1'b0}}, Content_counter_2};  // Bit_Extender bit_extender_2
  cu_I cu_i_1 (
    .OPC3(bitselector_2_out[3]), .OPC2(bitselector_2_out[2]), .OPC1(bitselector_2_out[1]),
    .OPC0(bitselector_2_out[0]), .SC2(Content_counter_2[2]), .SC1(Content_counter_2[1]),
    .SC0(Content_counter_2[0]), .C0(cu_i_1_c0), .C1(cu_i_1_c1), .C2(cu_i_1_c2), .C3(cu_i_1_c3),
    .C4(cu_i_1_c4), .C5(cu_i_1_c5), .C6(cu_i_1_c6), .C7(cu_i_1_c7), .C8(cu_i_1_c8), .C9(cu_i_1_c9),
    .C10(cu_i_1_c10), .C11(cu_i_1_c11));
  CU_II cu_ii_1 (
    .OPC3(bitselector_2_out[3]), .OPC2(bitselector_2_out[2]), .OPC1(bitselector_2_out[1]),
    .OPC0(bitselector_2_out[0]), .SC2(Content_counter_2[2]), .SC1(Content_counter_2[1]),
    .SC0(Content_counter_2[0]), .c12(cu_ii_1_c12), .c13(cu_ii_1_c13), .c14(cu_ii_1_c14), .c15(cu_ii_1_c15));
  Decimal_decoudeur Decimal_Decoder_6 (.Din(bit_extender_2_out), .Dout(Decimal_Decoder_6_dout));
  _7_Segment_Display u_7_segment_display_18 (
    .g(Decimal_Decoder_6_dout[3]), .f(Decimal_Decoder_6_dout[2]), .a(Decimal_Decoder_6_dout[1]),
    .b(Decimal_Decoder_6_dout[0]), .e(Decimal_Decoder_6_dout[19]), .d(Decimal_Decoder_6_dout[18]),
    .c(Decimal_Decoder_6_dout[17]), .dp(Decimal_Decoder_6_dout[16]));

  // Notes on the sheet:
  //   ALU
  //   Internal Address Bus(4Bits)
  //   Data Bus
  //   External Address BUS
  //   External Data BUS
  //   c11
  //   c15
  //   c14
  //   c0
  //   c13
  //   c9
  //   c8
  //   c12
  //   c7
  //   c5
  //   c3
  //   c1
  //   Step Counter
  //   c10
  //   c6
  //   c4
  //   c2
  //   CU1
  //   CU2
endmodule

module Memory_cell (
  input  Clock,
  input  WE,
  input  Din,
  input  OE,
  input  Reset,
  output Dout,
  output Stored_Data
);

  wire and_1_out, and_2_out, not_1_out, or_1_out;

  not not_1 (not_1_out, WE);
  and and_1 (and_1_out, Stored_Data, not_1_out);
  and and_2 (and_2_out, WE, Din);
  or or_1 (or_1_out, and_1_out, and_2_out);
  D_Flip_Flop_part d_ff_1 (.clk(Clock), .D(or_1_out), .Q(Stored_Data), .reset(Reset));  // open: Qn, preset, en
  assign Dout = OE ? Stored_Data : 1'bz;  // Controlled_Buffer controlled_buffer_1

  // Notes on the sheet:
  //   Cellule Mémoire
endmodule

module Registre (
  input  Clock,
  input  WE,
  input  [7:0] Din,
  input  OE,
  output [7:0] Dout,
  output [7:0] Stored_Data
);

  Memory_cell _0 (
    .Clock(Clock), .WE(WE), .Din(Din[0]), .OE(OE), .Dout(Dout[0]), .Stored_Data(Stored_Data[0]));  // open: Reset
  Memory_cell _1 (
    .Clock(Clock), .WE(WE), .Din(Din[1]), .OE(OE), .Dout(Dout[1]), .Stored_Data(Stored_Data[1]));  // open: Reset
  Memory_cell _2 (
    .Clock(Clock), .WE(WE), .Din(Din[2]), .OE(OE), .Dout(Dout[2]), .Stored_Data(Stored_Data[2]));  // open: Reset
  Memory_cell _3 (
    .Clock(Clock), .WE(WE), .Din(Din[3]), .OE(OE), .Dout(Dout[3]), .Stored_Data(Stored_Data[3]));  // open: Reset
  Memory_cell _4 (
    .Clock(Clock), .WE(WE), .Din(Din[4]), .OE(OE), .Dout(Dout[4]), .Stored_Data(Stored_Data[4]));  // open: Reset
  Memory_cell _5 (
    .Clock(Clock), .WE(WE), .Din(Din[5]), .OE(OE), .Dout(Dout[5]), .Stored_Data(Stored_Data[5]));  // open: Reset
  Memory_cell _6 (
    .Clock(Clock), .WE(WE), .Din(Din[6]), .OE(OE), .Dout(Dout[6]), .Stored_Data(Stored_Data[6]));  // open: Reset
  Memory_cell _7 (
    .Clock(Clock), .WE(WE), .Din(Din[7]), .OE(OE), .Dout(Dout[7]), .Stored_Data(Stored_Data[7]));  // open: Reset

  // Notes on the sheet:
  //   Registre (8 bits)
endmodule

module \Addresse_Mémoire_Registre  (
  input  Clock,
  input  WE,
  input  [3:0] Din,
  input  OE,
  output [3:0] Dout,
  output [3:0] Stored_Data
);

  Memory_cell _0 (
    .Clock(Clock), .WE(WE), .Din(Din[0]), .OE(OE), .Dout(Dout[0]), .Stored_Data(Stored_Data[0]));  // open: Reset
  Memory_cell _1 (
    .Clock(Clock), .WE(WE), .Din(Din[1]), .OE(OE), .Dout(Dout[1]), .Stored_Data(Stored_Data[1]));  // open: Reset
  Memory_cell _2 (
    .Clock(Clock), .WE(WE), .Din(Din[2]), .OE(OE), .Dout(Dout[2]), .Stored_Data(Stored_Data[2]));  // open: Reset
  Memory_cell _3 (
    .Clock(Clock), .WE(WE), .Din(Din[3]), .OE(OE), .Dout(Dout[3]), .Stored_Data(Stored_Data[3]));  // open: Reset

  // Notes on the sheet:
  //   Addresse Mémoire Registre
endmodule

module Adder (
  input  A,
  input  B,
  input  Cin,
  output S,
  output Cout
);

  wire and_1_out, and_2_out, xor_1_out;

  xor xor_1 (xor_1_out, A, B);
  xor xor_2 (S, xor_1_out, Cin);
  and and_1 (and_1_out, xor_1_out, Cin);
  and and_2 (and_2_out, A, B);
  or or_1 (Cout, and_1_out, and_2_out);

  // Notes on the sheet:
  //   Addar 1bits
endmodule

module Full_Adder (
  input  Cin,
  input  A0,
  input  B0,
  input  A1,
  input  B1,
  input  A2,
  input  B2,
  input  A3,
  input  B3,
  input  A4,
  input  B4,
  input  A5,
  input  B5,
  input  A6,
  input  B6,
  input  A7,
  input  B7,
  output [7:0] S,
  output R
);

  wire adder_1_cout, adder_2_cout, adder_3_cout, adder_4_cout, adder_5_cout, adder_6_cout, adder_7_cout;

  Adder adder_1 (.A(A0), .B(B0), .S(S[0]), .Cin(Cin), .Cout(adder_1_cout));
  Adder adder_2 (.A(A1), .B(B1), .S(S[1]), .Cin(adder_1_cout), .Cout(adder_2_cout));
  Adder adder_3 (.A(A2), .B(B2), .S(S[2]), .Cin(adder_2_cout), .Cout(adder_3_cout));
  Adder adder_4 (.A(A3), .B(B3), .S(S[3]), .Cin(adder_3_cout), .Cout(adder_4_cout));
  Adder adder_5 (.A(A4), .B(B4), .S(S[4]), .Cin(adder_4_cout), .Cout(adder_5_cout));
  Adder adder_6 (.A(A5), .B(B5), .S(S[5]), .Cin(adder_5_cout), .Cout(adder_6_cout));
  Adder adder_7 (.A(A6), .B(B6), .S(S[6]), .Cin(adder_6_cout), .Cout(adder_7_cout));
  Adder adder_8 (.A(A7), .B(B7), .S(S[7]), .Cin(adder_7_cout), .Cout(R));

  // Notes on the sheet:
  //   Full Adder
endmodule

module _1_bit_selec (
  input  A,
  input  B,
  input  Select,
  output Result
);

  wire and_1_out, and_2_out, not_1_out;

  not not_1 (not_1_out, Select);
  and and_1 (and_1_out, A, not_1_out);
  and and_2 (and_2_out, B, Select);
  or or_1 (Result, and_1_out, and_2_out);
endmodule

module _8_bit_selec (
  input  [7:0] A,
  input  [7:0] B,
  input  in_3,
  output [7:0] Resultat
);

  _1_bit_selec u_1_bit_selec_1 (.A(A[0]), .Result(Resultat[0]), .B(B[0]), .Select(in_3));
  _1_bit_selec u_1_bit_selec_2 (.A(A[1]), .Result(Resultat[1]), .B(B[1]), .Select(in_3));
  _1_bit_selec u_1_bit_selec_3 (.A(A[2]), .Result(Resultat[2]), .B(B[2]), .Select(in_3));
  _1_bit_selec u_1_bit_selec_4 (.A(A[3]), .Result(Resultat[3]), .B(B[3]), .Select(in_3));
  _1_bit_selec u_1_bit_selec_5 (.A(A[4]), .Result(Resultat[4]), .B(B[4]), .Select(in_3));
  _1_bit_selec u_1_bit_selec_6 (.A(A[5]), .Result(Resultat[5]), .B(B[5]), .Select(in_3));
  _1_bit_selec u_1_bit_selec_7 (.A(A[6]), .Result(Resultat[6]), .B(B[6]), .Select(in_3));
  _1_bit_selec _1_bit_selec (.A(A[7]), .Result(Resultat[7]), .B(B[7]), .Select(in_3));
endmodule

module D_Flip_Flop (
  input  Preset,
  input  D,
  input  Clear,
  output Q,
  output Q_prime
);

  wire clock_1_out, nand_1_out, nand_2_out, not_1_out;

  Clock clock_1 (.out(clock_1_out));
  not not_1 (not_1_out, D);
  nand nand_1 (nand_1_out, D, clock_1_out, Clear);
  nand nand_2 (nand_2_out, Preset, clock_1_out, not_1_out);
  nand nand_3 (Q, Preset, nand_1_out, Q_prime);
  nand nand_4 (Q_prime, Q, nand_2_out, Clear);
endmodule

module Shift_registre (
  input  [3:0] Data,
  input  Load,
  input  CLK,
  input  Clear,
  input  Preset
);

  wire and_1_out, and_2_out, and_3_out, and_4_out, and_5_out, and_6_out, and_7_out, and_8_out, d_ff_1_p6,
       d_ff_2_p6, d_ff_3_p6, d_ff_4_p6, not_1_out, or_1_out, or_2_out, or_3_out, or_4_out;

  not not_1 (not_1_out, Load);
  and and_1 (and_1_out, Data[0], Load);
  and and_2 (and_2_out, not_1_out, d_ff_1_p6);
  or or_1 (or_1_out, and_1_out, and_2_out);
  and and_3 (and_3_out, Data[1], Load);
  // D_Flip_Flop d_ff_1: pin names not known; wires that end beside it: or_1_out, CLK, Preset, Preset, Clear, d_ff_1_p6
  and and_4 (and_4_out, not_1_out, d_ff_2_p6);
  or or_2 (or_2_out, and_3_out, and_4_out);
  // D_Flip_Flop d_ff_2: pin names not known; wires that end beside it: or_2_out, CLK, Preset, Preset, Clear, d_ff_2_p6
  and and_5 (and_5_out, Data[2], Load);
  and and_6 (and_6_out, not_1_out, d_ff_3_p6);
  or or_3 (or_3_out, and_5_out, and_6_out);
  // D_Flip_Flop d_ff_3: pin names not known; wires that end beside it: or_3_out, CLK, Preset, Preset, Clear, d_ff_3_p6
  and and_7 (and_7_out, Data[3], Load);
  or or_4 (or_4_out, and_7_out, and_8_out);
  and and_8 (and_8_out, not_1_out, d_ff_4_p6);
  // D_Flip_Flop d_ff_4: pin names not known; wires that end beside it: or_4_out, CLK, Preset, Preset, Clear, d_ff_4_p6
endmodule

module ALU (
  input  OE,
  input  [7:0] Reg_A,
  input  [7:0] Reg_B,
  output [7:0] Dout,
  output [7:0] ALU_Result,
  output Carry_Out
);

  Full_Adder full_adder_1 (
    .Cin(1'b0), .A0(Reg_A[0]), .B0(Reg_B[0]), .A1(Reg_A[1]), .B1(Reg_B[1]), .A2(Reg_A[2]), .B2(Reg_B[2]),
    .A3(Reg_A[3]), .B3(Reg_B[3]), .A4(Reg_A[4]), .B4(Reg_B[4]), .A5(Reg_A[5]), .B5(Reg_B[5]), .A6(Reg_A[6]),
    .B6(Reg_B[6]), .A7(Reg_A[7]), .B7(Reg_B[7]), .R(Carry_Out), .S(ALU_Result));
  assign Dout = OE ? ALU_Result : 8'bz;  // Controlled_Buffer controlled_buffer_1

  // Notes on the sheet:
  //   ALU 8 BITS
  //   Full Adder
endmodule

module PC_Compteur (
  input  Counter_OE,
  input  [3:0] Data,
  input  [3:0] Content_of_counter,
  input  Counter_Enable,
  input  CLK,
  output [3:0] out_6
);

  Counter #(.width(4), .max('h2)) counter_1 (
    .D(Data), .count(Counter_Enable), .Q(Content_of_counter), .clk(CLK));  // open: load, carry, clr
  assign out_6 = Counter_OE ? Content_of_counter : 4'bz;  // Controlled_Buffer controlled_buffer_1

  // Notes on the sheet:
  //   PC
endmodule

module Decimal_decoudeur (
  input  [7:0] Din,
  output [31:0] Dout
);

  ROM #(.dataWidth(32)) rom_1 (
    .addr(Din),
    .data({Dout[31:28], Dout[15:12], Dout[27:24], Dout[11:8], Dout[23:20], Dout[7:4], Dout[19:16], Dout[3:0]}));  // open: sel

  // Notes on the sheet:
  //   contents of rom_1 (hex, n*v repeats v):
  //   e7 21 cb 6b 2d 6e ee 23 ef 2f 21e7 2121 21cb 216b 212d 216e 21ee 2123 21ef 212f cbe7 cb21 cbcb cb6b
  //   cb2d cb6e cbee cb23 cbef cb2f 6be7 6b21 6bcb 6b6b 6b2d 6b6e 6bee 6b23 6bef 6b2f 2de7 2d21 2dcb 2d6b
  //   2d2d 2d6e 2dee 2d23 2def 2d2f 6ee7 6e21 6ecb 6e6b 6e2d 6e6e 6eee 6e23 6eef 6e2f eee7 ee21 eecb ee6b
  //   ee2d ee6e eeee ee23 eeef ee2f 23e7 2321 23cb 236b 232d 236e 23ee 2323 23ef 232f efe7 ef21 efcb ef6b
  //   ef2d ef6e efee ef23 efef ef2f 2fe7 2f21 2fcb 2f6b 2f2d 2f6e 2fee 2f23 2fef 2f2f 21e7e7 21e721 21e7cb
  //   21e76b 21e72d 21e76e 21e7ee 21e723 21e7ef 21e72f 2121e7 212121 2121cb 21216b 21212d 21216e 2121ee
  //   212123 2121ef 21212f 21cbe7 21cb21 21cbcb 21cb6b 21cb2d 21cb6e 21cbee 21cb23 21cbef 21cb2f 216be7
  //   216b21 216bcb 216b6b 216b2d 216b6e 216bee 216b23 216bef 216b2f 212de7 212d21 212dcb 212d6b 212d2d
  //   212d6e 212dee 212d23 212def 212d2f 216ee7 216e21 216ecb 216e6b 216e2d 216e6e 216eee 216e23 216eef
  //   216e2f 21eee7 21ee21 21eecb 21ee6b 21ee2d 21ee6e 21eeee 21ee23 21eeef 21ee2f 2123e7 212321 2123cb
  //   21236b 21232d 21236e 2123ee 212323 2123ef 21232f 21efe7 21ef21 21efcb 21ef6b 21ef2d 21ef6e 21efee
  //   21ef23 21efef 21ef2f 212fe7 212f21 212fcb 212f6b 212f2d 212f6e 212fee 212f23 212fef 212f2f cbe7e7
  //   cbe721 cbe7cb cbe76b cbe72d cbe76e cbe7ee cbe723 cbe7ef cbe72f cb21e7 cb2121 cb21cb cb216b cb212d
  //   cb216e cb21ee cb2123 cb21ef cb212f cbcbe7 cbcb21 cbcbcb cbcb6b cbcb2d cbcb6e cbcbee cbcb23 cbcbef
  //   cbcb2f cb6be7 cb6b21 cb6bcb cb6b6b cb6b2d cb6b6e cb6bee cb6b23 cb6bef cb6b2f cb2de7 cb2d21 cb2dcb
  //   cb2d6b cb2d2d cb2d6e cb2dee cb2d23 cb2def cb2d2f cb6ee7 cb6e21 cb6ecb cb6e6b cb6e2d cb6e6e
  //   Decimal Decodeur
endmodule

module Flip_Flop (
  input  D,
  input  reset4,
  input  CLK,
  input  Enable,
  output Q
);

  wire and_1_out, and_2_out, nand_1_out, nand_2_out, nand_4_out, not_1_out, not_2_out, not_3_out, or_1_out,
       or_2_out, or_3_out;

  not not_1 (not_1_out, reset4);
  or or_1 (or_1_out, reset4, Enable);
  not not_2 (not_2_out, or_1_out);
  and and_1 (and_1_out, not_2_out, Q);
  and and_2 (and_2_out, D, not_1_out, or_1_out);
  or or_2 (or_2_out, and_2_out, and_1_out);
  not not_3 (not_3_out, or_2_out);
  or or_3 (or_3_out, CLK, reset4);
  nand nand_1 (nand_1_out, or_2_out, or_3_out);
  nand nand_2 (nand_2_out, or_3_out, not_3_out);
  nand nand_3 (Q, nand_1_out, nand_4_out);
  nand nand_4 (nand_4_out, Q, nand_2_out);
endmodule

module Resttable__Flip_Flop (
  input  Clk,
  input  D,
  input  Enable,
  output Q
);

  wire and_1_out;

  and and_1 (and_1_out, D, Enable);
  Flip_Flop flip_flop_1 (.Enable(and_1_out), .Q(Q));  // open: reset4, D, CLK
endmodule

module Test (
  input  Enable,
  input  Reset,
  input  D,
  input  clk,
  input  Output_enable,
  output Q,
  output Stored__Data
);

  Flip_Flop flip_flop_1 (.Enable(Enable), .reset4(Reset), .D(D), .CLK(clk), .Q(Stored__Data));
  assign Q = Output_enable ? Stored__Data : 1'bz;  // Controlled_Buffer controlled_buffer_1
endmodule

module cu_I (
  input  OPC3,
  input  OPC2,
  input  OPC1,
  input  OPC0,
  input  SC2,
  input  SC1,
  input  SC0,
  output C0,
  output C1,
  output C2,
  output C3,
  output C4,
  output C5,
  output C6,
  output C7,
  output C8,
  output C9,
  output C10,
  output C11
);

  wire and_3_out, and_4_out, and_5_out, and_6_out, and_7_out, and_8_out, and_10_out, and_11_out, and_12_out,
       and_13_out, and_14_out, and_15_out, and_16_out, and_18_out, and_19_out, not_1_out, not_2_out,
       not_3_out, not_4_out, not_5_out, not_6_out, not_7_out, not_8_out, not_9_out, not_10_out, not_11_out,
       not_12_out, not_13_out, not_14_out, not_15_out, not_16_out, not_17_out, not_18_out, not_19_out,
       not_20_out, not_21_out, not_22_out, not_23_out, not_24_out, not_25_out, not_26_out, not_27_out,
       not_28_out, not_29_out, not_30_out, not_31_out, not_32_out, not_33_out, not_34_out, not_35_out,
       not_36_out, not_37_out, not_38_out, not_39_out, not_40_out, not_41_out, not_42_out, not_43_out,
       not_44_out;

  not not_1 (not_1_out, SC2);
  not not_2 (not_2_out, SC1);
  not not_3 (not_3_out, SC0);
  not not_4 (not_4_out, SC2);
  not not_5 (not_5_out, SC1);
  not not_6 (not_6_out, SC2);
  not not_7 (not_7_out, SC1);
  not not_8 (not_8_out, OPC1);
  not not_9 (not_9_out, SC1);
  not not_10 (not_10_out, SC0);
  not not_11 (not_11_out, SC2);
  not not_12 (not_12_out, SC1);
  not not_13 (not_13_out, OPC1);
  not not_14 (not_14_out, SC1);
  not not_15 (not_15_out, SC0);
  not not_16 (not_16_out, SC2);
  not not_17 (not_17_out, SC0);
  not not_18 (not_18_out, OPC1);
  not not_19 (not_19_out, SC1);
  not not_20 (not_20_out, SC2);
  not not_21 (not_21_out, SC0);
  not not_22 (not_22_out, OPC1);
  not not_23 (not_23_out, SC2);
  not not_24 (not_24_out, SC2);
  not not_25 (not_25_out, SC2);
  not not_26 (not_26_out, SC1);
  not not_27 (not_27_out, SC0);
  not not_28 (not_28_out, OPC1);
  not not_29 (not_29_out, SC2);
  not not_30 (not_30_out, SC2);
  not not_31 (not_31_out, SC2);
  not not_32 (not_32_out, SC1);
  not not_33 (not_33_out, OPC1);
  not not_34 (not_34_out, SC1);
  not not_35 (not_35_out, SC0);
  not not_36 (not_36_out, OPC0);
  not not_37 (not_37_out, SC2);
  and and_1 (C0, not_1_out, not_2_out, not_3_out);
  and and_2 (C1, not_4_out, not_5_out, SC0);
  and and_3 (and_3_out, not_6_out, not_7_out, SC0);
  and and_4 (and_4_out, not_8_out, SC2, not_9_out, not_10_out);
  and and_5 (and_5_out, not_11_out, not_12_out, SC0);
  and and_6 (and_6_out, not_13_out, SC2, not_14_out, not_15_out);
  not not_38 (not_38_out, SC2);
  and and_7 (and_7_out, not_16_out, SC1, not_17_out);
  and and_8 (and_8_out, not_18_out, SC2, not_19_out, SC0);
  and and_9 (C7, not_20_out, SC1, not_21_out);
  and and_10 (and_10_out, not_22_out, not_23_out, SC1, SC0);
  and and_11 (and_11_out, OPC0, not_24_out, SC1, SC0);
  and and_12 (and_12_out, not_25_out, not_26_out, not_27_out);
  and and_13 (and_13_out, not_28_out, not_29_out, SC1, SC0);
  and and_14 (and_14_out, OPC0, not_30_out, SC1, SC0);
  and and_15 (and_15_out, not_31_out, not_32_out, SC0);
  and and_16 (and_16_out, not_33_out, SC2, not_34_out, not_35_out);
  and and_17 (C11, OPC1, not_36_out, not_37_out, SC1, SC0);
  not not_39 (not_39_out, SC1);
  or or_1 (C3, and_3_out, and_4_out);
  or or_2 (C5, and_7_out, and_8_out);
  not not_40 (not_40_out, SC0);
  not not_41 (not_41_out, SC1);
  or or_3 (C8, and_10_out, and_11_out);
  or or_4 (C9, and_12_out, and_13_out, and_14_out);
  not not_42 (not_42_out, SC1);
  not not_43 (not_43_out, SC0);
  not not_44 (not_44_out, SC1);
  and and_18 (and_18_out, OPC0, OPC1, SC0, not_38_out);
  and and_19 (and_19_out, OPC0, SC2, not_42_out, not_43_out);
  and and_20 (C2, not_44_out, OPC1, OPC0, SC2, not_39_out);
  or or_5 (C4, and_5_out, and_6_out, and_18_out);
  and and_21 (C6, not_40_out, OPC1, OPC0, SC2, not_41_out);
  or or_6 (C10, and_15_out, and_16_out, and_19_out);
endmodule

module CU_II (
  input  OPC3,
  input  OPC2,
  input  OPC1,
  input  OPC0,
  input  SC2,
  input  SC1,
  input  SC0,
  output c12,
  output c13,
  output c14,
  output c15
);

  wire not_1_out, not_2_out, not_3_out, not_4_out, not_5_out, not_6_out, not_7_out, not_8_out;

  not not_1 (not_1_out, OPC1);
  not not_2 (not_2_out, OPC0);
  not not_3 (not_3_out, SC1);
  not not_4 (not_4_out, SC1);
  not not_5 (not_5_out, OPC0);
  not not_6 (not_6_out, SC2);
  and and_1 (c12, not_1_out, not_2_out, SC2, not_3_out, SC0);
  not not_7 (not_7_out, OPC1);
  not not_8 (not_8_out, SC2);
  and and_2 (c13, not_7_out, SC2, OPC0, not_4_out, SC0);
  and and_3 (c14, OPC1, OPC0, not_8_out, SC1, SC0);
  and and_4 (c15, not_5_out, not_6_out, SC1, SC0);
endmodule
